// Digital circuit COMPUTER.dig as structural Verilog
module COMPUTER (
  input  CLK,
  input  [15:0] INSTR
);

  wire ctrl_unit_1_op2sel, ctrl_unit_1_rwe;
  wire [2:0] ctrl_unit_1_alop, ctrl_unit_1_rda, ctrl_unit_1_rsa1, ctrl_unit_1_rsa2;
  wire [7:0] _8_register_bank_1_p4, _8_register_bank_1_p7, _8_register_bank_1_p8, ctrl_unit_1_op2im,
       multiplexer_1_out;

  CTRL_UNIT ctrl_unit_1 (
    .INSTR(INSTR), .RSA1(ctrl_unit_1_rsa1), .RSA2(ctrl_unit_1_rsa2), .RDA(ctrl_unit_1_rda),
    .RWE(ctrl_unit_1_rwe), .ALOP(ctrl_unit_1_alop), .OP2Sel(ctrl_unit_1_op2sel), .OP2Im(ctrl_unit_1_op2im));  // open: RDSrc, MemWE, PCNext
  // _8_REGISTER_BANK _8_register_bank_1: pin names not known; wires that end beside it: ctrl_unit_1_rsa1, ctrl_unit_1_rsa2, ctrl_unit_1_rda, _8_register_bank_1_p4, ctrl_unit_1_rwe, CLK, _8_register_bank_1_p7, _8_register_bank_1_p8
  Multiplexer #(.Bits(8)) multiplexer_1 (
    .sel(ctrl_unit_1_op2sel), .in_0(_8_register_bank_1_p8), .in_1(ctrl_unit_1_op2im), .out(multiplexer_1_out));
  _256_INSTR_MEM _256_instr_mem_1 ();  // open: A, WD, WE, CLK, RD
  ALU_8 alu_8_1 (.A(_8_register_bank_1_p7), .B(multiplexer_1_out), .OP(ctrl_unit_1_alop), .S(_8_register_bank_1_p4));
endmodule
